# Fritzing sketch sketch_part1 (saved by Fritzing 0.9.3b)
breadboards: 1

parts:
  Part1 = Arduino Uno (Rev3) - ICSP
  LED1 = RGB LED (com. anode, rbg) [package="5 mm [THT]"]
  R1 = Resistor [tolerance=±5% resistance=220 package="1206 [SMD]"]
  R2 = PHOTOCELL [package=photocell-kit]
  R3 = Resistor [tolerance=±5% resistance=10k package="2010 [SMD]"]

nets:
  N1: Part1.A0, R2.P$2, R3.Pin_0
  N2: Part1.GND, R1.Pin_1, R2.P$1, R3.Pin_1
  N3: Part1.D11_PWM/MOSI, LED1.common_anode
  N4: LED1.green_cathode, R1.Pin_0
