# Fritzing sketch sketch_part2 (saved by Fritzing 0.9.3b)
breadboards: 1

parts:
  Part2 = Arduino Uno (Rev3) - ICSP
  HC-SR04_Sensor_1 = HC-SR04 Ultrasonic Distance Sensor
  R1 = PHOTOCELL [package=photocell-kit]
  R2 = Resistor [tolerance=±5% resistance=10k package="2010 [SMD]"]
  LED1 = RGB LED (com. anode, rbg) [package="5 mm [THT]"]
  R5 = Resistor [tolerance=±5% resistance=220 package="2010 [SMD]"]
  R4 = Resistor [tolerance=±5% resistance=220 package="2010 [SMD]"]
  R3 = Resistor [tolerance=±5% resistance=220 package="2010 [SMD]"]

nets:
  N1: Part2.A0, R1.P$1, R2.Pin_1
  5V: Part2.5V, HC-SR04_Sensor_1.VCC, R1.P$2
  N2: Part2.D8, HC-SR04_Sensor_1.ECHO
  N3: Part2.D11_PWM/MOSI, LED1.blue_cathode
  GND: Part2.GND, HC-SR04_Sensor_1.GND, R2.Pin_0
  N4: Part2.D3_PWM, R3.Pin_0
  N5: Part2.D4, R4.Pin_0
  N6: Part2.D5_PWM, R5.Pin_0
  N7: Part2.D7, HC-SR04_Sensor_1.TRIG
  N8: LED1.red_cathode, R5.Pin_1
  N9: LED1.common_anode, R4.Pin_1
  N10: LED1.green_cathode, R3.Pin_1
